// Logisim project Final_Project.circ as structural Verilog: 13 circuits, main circuit main
module main (
  input  ResetD,
  input  ResetC
);

  wire clk, DWE, SUB, WE;
  wire [1:0] AFS, RSS;
  wire [2:0] Reg_D, RegRA, RegRb;
  wire [3:0] alu_1_aluout, DataIn, Port_A, Port_B, pro_prom_1_data, pro_prom_1_opcode;
  wire [7:0] binary_counter_1_promadd;

  Clock clock_1 (.out(clk));
  Binary_Counter binary_counter_1 (.Reset(ResetC), .clk(clk), .PromAdd(binary_counter_1_promadd));
  Pro_PROM pro_prom_1 (
    .Address(binary_counter_1_promadd), .Data(pro_prom_1_data), .RegRB(RegRb), .RegRA(RegRA), .Reg_D(Reg_D),
    .Opcode(pro_prom_1_opcode));
  Decoder_PROM decoder_prom_1 (.Opcode(pro_prom_1_opcode), .WE(WE), .DWE(DWE), .RSS(RSS), .AFS(AFS), .SUB(SUB));
  Multiplexer #(.select(2), .width(4), .enable("false")) multiplexer_1 (
    .in0(pro_prom_1_data), .in1(alu_1_aluout), .in2(Port_A), .out(DataIn), .sel(RSS));  // open: in3
  TTY tty_1 (.data({Port_A[2:0], Port_B}), .clk(clk), .we(DWE), .clr(ResetD));
  Reg_3Port reg_3port_1 (
    .WE(WE), .Addr_D(Reg_D), .CLK(clk), .Addr_A(RegRA), .Addr_B(RegRb), .DataIn(DataIn), .Port_A(Port_A),
    .Port_B(Port_B));
  ALU alu_1 (.A(Port_A), .B(Port_B), .SUB(SUB), .AFS(AFS), .ALUout(alu_1_aluout));

  // Other names for the same wires on the sheet: R = ResetC
endmodule

module Binary_Counter (
  input  Reset,
  input  clk,
  output [7:0] PromAdd
);

  Counter counter_1 (.clr(Reset), .load(1'b0), .up(1'b1), .count(1'b1), .clk(clk), .Q(PromAdd));  // open: D, carry
endmodule

module Pro_PROM (
  input  [7:0] Address,
  output [3:0] Data,
  output [2:0] RegRB,
  output [2:0] RegRA,
  output [2:0] Reg_D,
  output [3:0] Opcode
);

  wire [11:7] rom_1_data;

  ROM #(.dataWidth(16)) rom_1 (.addr(Address), .data({Opcode, rom_1_data[11], Reg_D, rom_1_data[7], RegRA, Data}));

  assign RegRB = Data[2:0];

  // Notes on the sheet:
  //   contents of rom_1 (hex, n*v repeats v):
  //   1202 1007 1102 1203 1307 3023 1402 1500 3045 1602 170d 3067 1302 1400 3034 1503 1602 3056 1302 1400
  //   3034 1503 160d 3056 1302 1400 3034 170f 1401 4617 7546 7305 3023 1600 170a 3067
endmodule

module Reg_3Port (
  input  WE,
  input  [2:0] Addr_D,
  input  CLK,
  input  [2:0] Addr_A,
  input  [2:0] Addr_B,
  input  [3:0] DataIn,
  output [3:0] Port_A,
  output [3:0] Port_B
);

  wire D0, D1, D2, D3, D4, D5, D6, D7;
  wire [3:0] M0, M1, M2, M3, M4, M5, M6, M7;

  Decoder #(.select(3)) decoder_1 (
    .out0(D0), .out1(D1), .out2(D2), .out3(D3), .out4(D4), .out5(D5), .out6(D6), .out7(D7), .sel(Addr_D),
    .en(WE));
  Register #(.width(4)) register_1 (.D(DataIn), .en(D0), .clk(CLK), .Q(M0));  // open: clr
  Register #(.width(4)) register_2 (.D(DataIn), .en(D1), .clk(CLK), .Q(M1));  // open: clr
  Register #(.width(4)) register_3 (.D(DataIn), .en(D2), .clk(CLK), .Q(M2));  // open: clr
  Register #(.width(4)) register_4 (.D(DataIn), .en(D3), .clk(CLK), .Q(M3));  // open: clr
  Register #(.width(4)) register_5 (.D(DataIn), .en(D4), .clk(CLK), .Q(M4));  // open: clr
  Register #(.width(4)) register_6 (.D(DataIn), .en(D5), .clk(CLK), .Q(M5));  // open: clr
  Register #(.width(4)) register_7 (.D(DataIn), .en(D6), .clk(CLK), .Q(M6));  // open: clr
  Register #(.width(4)) register_8 (.D(DataIn), .en(D7), .clk(CLK), .Q(M7));  // open: clr
  Multiplexer #(.select(3), .width(4), .enable("false")) multiplexer_1 (
    .in0(M0), .in1(M1), .in2(M2), .in3(M3), .in4(M4), .in5(M5), .in6(M6), .in7(M7), .out(Port_A), .sel(Addr_A));
  Multiplexer #(.select(3), .width(4), .enable("false")) multiplexer_2 (
    .in0(M0), .in1(M1), .in2(M2), .in3(M3), .in4(M4), .in5(M5), .in6(M6), .in7(M7), .out(Port_B), .sel(Addr_B));

  // Other names for the same wires on the sheet: AR[2:0] = Addr_A; BR[2:0] = Addr_B; D[3:0] = DataIn
endmodule

module MUX (
  input  [3:0] PROM,
  input  [3:0] ALU,
  input  [3:0] RegOut,
  input  [1:0] RSS,
  output [3:0] DataOut
);

  Multiplexer #(.select(2), .width(4), .enable("false")) multiplexer_1 (
    .in0(PROM), .in1(ALU), .in2(RegOut), .out(DataOut), .sel(RSS));  // open: in3
endmodule

module Decoder_PROM (
  input  [3:0] Opcode,
  output WE,
  output DWE,
  output [1:0] RSS,
  output [1:0] AFS,
  output SUB
);

  ROM #(.addrWidth(4), .dataWidth(7)) rom_1 (.addr(Opcode), .data({SUB, AFS, RSS, DWE, WE}));

  // Notes on the sheet:
  //   contents of rom_1 (hex, n*v repeats v):
  //   0 1 9 2 5 15 25 35 7*0 75
endmodule

module ALU (
  input  [3:0] A,
  input  [3:0] B,
  input  SUB,
  input  [1:0] AFS,
  output [3:0] ALUout
);

  wire [3:0] add_4bit_1_addout, and_4bit_1_andout, or_4bit_1_orout, xor_4bit_1_xorout;

  XOR_4bit xor_4bit_1 (.A(A), .B(B), .XORout(xor_4bit_1_xorout));
  AND_4bit and_4bit_1 (.A(A), .B(B), .ANDout(and_4bit_1_andout));
  OR_4bit or_4bit_1 (.A(A), .B(B), .ORout(or_4bit_1_orout));
  Add_4bit add_4bit_1 (.A(A), .B(B), .SUB(SUB), .ADDout(add_4bit_1_addout));
  Multiplexer #(.select(2), .width(4), .enable("false")) multiplexer_1 (
    .in0(xor_4bit_1_xorout), .in1(and_4bit_1_andout), .in2(or_4bit_1_orout), .in3(add_4bit_1_addout),
    .out(ALUout), .sel(AFS));
endmodule

module Add_1bit (
  input  A,
  input  B,
  input  Cin,
  output S,
  output Cout
);

  wire and_1_out, and_2_out, and_3_out;

  xor xor_1 (S, A, B, Cin);
  and and_1 (and_1_out, A, B);
  and and_2 (and_2_out, B, Cin);
  and and_3 (and_3_out, A, Cin);
  or or_1 (Cout, and_1_out, and_2_out, and_3_out);
endmodule

module Add_8bit (
  input  [7:0] A,
  input  [7:0] in_2
);

  wire C0, C1, C2, C3, C4, C5, C6, S0;

  Add_1bit add_1bit_1 (.A(A[0]), .B(in_2[0]), .Cin(1'b0), .S(S0), .Cout(C0));
  Add_1bit add_1bit_2 (.A(A[1]), .B(in_2[1]), .Cin(C0), .S(S0), .Cout(C1));
  Add_1bit add_1bit_3 (.A(A[2]), .B(in_2[2]), .Cin(C1), .Cout(C2));  // open: S
  Add_1bit add_1bit_4 (.A(A[3]), .B(in_2[3]), .Cin(C2), .Cout(C3));  // open: S
  Add_1bit add_1bit_5 (.A(A[4]), .B(in_2[4]), .Cin(C3), .Cout(C4));  // open: S
  Add_1bit add_1bit_6 (.A(A[5]), .B(in_2[5]), .Cin(C4), .Cout(C5));  // open: S
  Add_1bit add_1bit_7 (.A(A[6]), .B(in_2[6]), .Cin(C5), .Cout(C6));  // open: S
  Add_1bit add_1bit_8 (.A(A[7]), .B(in_2[7]), .Cin(C6));  // open: S, Cout

  // Other names for the same wires on the sheet: B0 = in_2[0]; B1 = in_2[1]; B2 = in_2[2]; B3 = in_2[3]; B4 = in_2[4];
  //   B5 = in_2[5]; B6 = in_2[6]; B7 = in_2[7]
endmodule

module Add_4bit (
  input  [3:0] A,
  input  [3:0] B,
  input  SUB,
  output [3:0] ADDout
);

  wire C0, C1, C2, xor_1_out, xor_2_out, xor_3_out, xor_4_out;

  xor xor_1 (xor_1_out, B[0], SUB);
  xor xor_2 (xor_2_out, B[1], SUB);
  xor xor_3 (xor_3_out, B[2], SUB);
  xor xor_4 (xor_4_out, B[3], SUB);
  Add_1bit add_1bit_1 (.A(A[0]), .B(xor_1_out), .Cin(SUB), .S(ADDout[0]), .Cout(C0));
  Add_1bit add_1bit_2 (.A(A[1]), .B(xor_2_out), .Cin(C0), .S(ADDout[1]), .Cout(C1));
  Add_1bit add_1bit_3 (.A(A[2]), .B(xor_3_out), .Cin(C1), .S(ADDout[2]), .Cout(C2));
  Add_1bit add_1bit_4 (.A(A[3]), .B(xor_4_out), .Cin(C2), .S(ADDout[3]));  // open: Cout
endmodule

module AND_4bit (
  input  [3:0] A,
  input  [3:0] B,
  output [3:0] ANDout
);

  and and_1 (ANDout[0], A[0], B[0]);
  and and_2 (ANDout[1], A[1], B[1]);
  and and_3 (ANDout[2], A[2], B[2]);
  and and_4 (ANDout[3], A[3], B[3]);
endmodule

module OR_4bit (
  input  [3:0] A,
  input  [3:0] B,
  output [3:0] ORout
);

  or or_1 (ORout[0], A[0], B[0]);
  or or_2 (ORout[1], A[1], B[1]);
  or or_3 (ORout[2], A[2], B[2]);
  or or_4 (ORout[3], A[3], B[3]);
endmodule

module XOR_4bit (
  input  [3:0] A,
  input  [3:0] B,
  output [3:0] XORout
);

  xor xor_1 (XORout[0], A[0], B[0]);
  xor xor_2 (XORout[1], A[1], B[1]);
  xor xor_3 (XORout[2], A[2], B[2]);
  xor xor_4 (XORout[3], A[3], B[3]);
endmodule
